# Fritzing sketch Sensor (saved by Fritzing 0.9.3b)
breadboards: 1

parts:
  Part1 = Arduino Pro Mini (3.3V)
  hc-sr1 = hc-sr04
  Adafruit_HUZZAH_ESP8266_Breakout1 = Adafruit HUZZAH ESP8266 Breakout [part_number=2471]
  LED1 = LEDs [package=led10mm]
  LED2 = LEDs [package=led10mm]
  LED3 = LEDs [package=led10mm]
  J1 = Piezo Speaker
  VCC1 = Battery block 9V

nets:
  VCC: Part1.VCC, hc-sr1.VCC, Adafruit_HUZZAH_ESP8266_Breakout1.V+
  N1: Part1.RAW, VCC1.+
  GND: Part1.GND, hc-sr1.GND, Adafruit_HUZZAH_ESP8266_Breakout1.GND, LED1.A, LED2.A, LED3.A, J1.pin1, VCC1.-
  N2: Part1.D9, hc-sr1.Echo
  N3: Part1.D8, hc-sr1.Trig
  N4: Part1.D7, LED3.C
  N5: Part1.D6, LED2.C
  N6: Part1.D5, LED1.C
  N7: Part1.D4, J1.pin2
  N8: Part1.D3, Adafruit_HUZZAH_ESP8266_Breakout1.RX
  N9: Part1.D2, Adafruit_HUZZAH_ESP8266_Breakout1.TX
